# Fritzing sketch workshop-next (saved by Fritzing 0.9.3b)
perfboards: 1

parts:
  U1 = attiny85 [package=dip]
  R1 = Photocell (LDR) [package=THT]
  R2 = Photocell (LDR) [package=THT]  # not connected
  R3 = Photocell (LDR) [package=THT]
  R4 = Photocell (LDR) [package=THT]  # not connected
  LED1 = prefix0000
  R5 = Resistor [tolerance=±5% resistance=220 package="0805 [SMD]"]
  R6 = Resistor [tolerance=±5% resistance=220 package="0805 [SMD]"]
  R7 = Resistor [tolerance=±5% resistance=220 package="0805 [SMD]"]  # not connected
  R8 = Resistor [tolerance=±5% resistance=220 package="0805 [SMD]"]

nets:
  N1: U1.Pin_3, R6.Pin_0
  N2: U1.Pin_4, R5.Pin_1
  N3: U1.Pin_5, LED1.connector2
  N4: U1.Pin_6, R8.Pin_0
  N5: U1.Pin_7, R5.Pin_0
  N6: U1.Pin_8, R1.pin_0, R3.pin_1
  N7: LED1.connector3, R6.Pin_1
