# Fritzing sketch workshop (saved by Fritzing 0.9.3b)
breadboards: 1

parts:
  Part1 = Arduino Uno (Rev3)
  R1 = PHOTOCELL [package=photocell]
  R2 = Resistor [tolerance=±5% resistance=220 package="0603 [SMD]"]
  CLIP1 = Alligator Clip
  CLIP2 = Alligator Clip
  CLIP3 = Alligator Clip
  CLIP4 = Alligator Clip
  CLIP5 = Alligator Clip
  CLIP6 = Alligator Clip

nets:
  N1: Part1.A5/SCL, R1.P$1, R2.Pin_1
  N2: Part1.5V, R1.P$2
  N3: Part1.GND, R2.Pin_0
  N4: CLIP1.wire, CLIP2.wire
  N5: CLIP3.wire, CLIP4.wire
  N6: CLIP5.wire, CLIP6.wire

custom parts:
  Alligator Clip: Alligator clip
  Alligator Clip: Alligator clip
  Alligator Clip: Alligator clip
